# Fritzing sketch nixieBoard (saved by Fritzing 0.9.3b)
circuit board: 20cm x 9cm
breadboards: 2

parts:
  IN-11-1 = IN-11 [package="DIP (Dual Inline) [THT]"]
  K155ID1-1 = IC, DIP package, 16 pins [chip_label=K155ID1]
  Raspberry_Pi_1 = Raspberry Pi Zero
  R1 = Resistor [tolerance=±5% resistance=15k package=THT]
  1361HVPS = double row female pin header, 12 pins [form="♀ (female)"]
  Power_plug1 = Power plug
  IN-11-2 = IN-11 [package="DIP (Dual Inline) [THT]"]
  K155ID1-2 = IC, DIP package, 16 pins [chip_label=K155ID1]
  R2 = Resistor [tolerance=±5% resistance=15k package=THT]

nets:
  N1: IN-11-1.V170, R1.Pin_0
  N2: IN-11-1.1, K155ID1-1.pin15
  N3: IN-11-1.2, K155ID1-1.pin8
  N4: IN-11-1.3, K155ID1-1.pin9
  N5: IN-11-1.4, K155ID1-1.pin13
  N6: IN-11-1.5, K155ID1-1.pin14
  N7: IN-11-1.6, K155ID1-1.pin11
  N8: IN-11-1.7, K155ID1-1.pin10
  N9: IN-11-1.8, K155ID1-1.pin1
  N10: IN-11-1.9, K155ID1-1.pin2
  N11: IN-11-1.0, K155ID1-1.pin16
  N12: K155ID1-1.pin3, Raspberry_Pi_1.pin_12
  N13: K155ID1-1.pin4, Raspberry_Pi_1.pin_24
  N14: K155ID1-1.pin5, Power_plug1.VCC, K155ID1-2.pin5
  N15: K155ID1-1.pin6, Raspberry_Pi_1.pin_18
  N16: K155ID1-1.pin7, Raspberry_Pi_1.pin_22
  N17: K155ID1-1.pin12, 1361HVPS.pin1, 1361HVPS.pin2, 1361HVPS.pin3, 1361HVPS.pin4, 1361HVPS.pin11, Power_plug1.GND, K155ID1-2.pin12
  N18: R1.Pin_1, 1361HVPS.pin12, R2.Pin_1
  N19: IN-11-2.V170, R2.Pin_0
  N20: IN-11-2.1, K155ID1-2.pin15
  N21: IN-11-2.2, K155ID1-2.pin8
  N22: IN-11-2.3, K155ID1-2.pin9
  N23: IN-11-2.4, K155ID1-2.pin13
  N24: IN-11-2.5, K155ID1-2.pin14
  N25: IN-11-2.6, K155ID1-2.pin11
  N26: IN-11-2.7, K155ID1-2.pin10
  N27: IN-11-2.8, K155ID1-2.pin1
  N28: IN-11-2.9, K155ID1-2.pin2
  N29: IN-11-2.0, K155ID1-2.pin16

custom parts:
  IN-11: An IN-11 bulb mounted With 16 pins on a 300mil dual inline package (DIP) footprint.
